# Fritzing sketch aula3_esquema (saved by Fritzing 1.0.2b)
breadboards: 1

parts:
  Mod1 = Raspberry Pi Pico
  U1 = POT [knob_status=50% power=0.5W package=alps_pot]
  LED1 = LED - 5mm [color="Red (633nm)" current=0.030A package="5 mm [THT]"]
  R1 = Resistor [tolerance=±5% power=0.25W resistance=100 package=THT]
  S1 = Pushbutton [package="[THT]"]
  J1 = Basic Servo
  Mod2 = Passive Buzzer

nets:
  N1: Mod1.pin_3, Mod1.pin_8, Mod1.pin_10, Mod1.pin_13, Mod1.pin_18, Mod1.pin_23, Mod1.pin_28, Mod1.pin_33, Mod1.pin_38, Mod1.pin_42, U1.E, U1.A, LED1.cathode, S1.Pin_1, S1.Pin_2, S1.Pin_3, S1.Pin_4, J1.gnd, Mod2.-
  N2: Mod1.pin_14, J1.pulse
  N3: Mod1.pin_27, R1.Pin_0
  N4: Mod1.pin_31, Mod2.S
  N5: Mod1.pin_32, U1.S
  N6: Mod1.pin_36, J1.vcc, Mod2.NC
  N7: LED1.anode, R1.Pin_1

notes:
  GP7 - Botão
  GP27 - Potenciômetro
  GP22- LED
  GP10 - Servo
  DigitalIO AnalogIO PWMIO
  Vermelho 3,3V
  Preto GND
  GP26 - Buzzer

custom parts:
  Raspberry Pi Pico: Raspberry Pi Pico. Based around the RP2040 microcontroller the Pico is a low cost microcontroller device bringing Raspberry Pi quality, cost, and easy of use to the microcontroller space. Jan 2021, Split part in to two versions: tht (this one) and SMD. This one will drill holes for a .1 in header in pcb to allow plugging in the module as well as providing pads to solder the module to the top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
