# Fritzing sketch Xiao_Neopixel (saved by Fritzing 1.0.2b)

parts:
  A1 = seeeduino-xiao
  U1 = WS2812 RGB LED matrix 8x8
  Componente1 = Thumb Joystick
  Mod1 = Passive Buzzer
  Componente2 = 14-segment LED Alphanumeric Backpack [part_number=1911]

nets:
  N1: A1.D0, Componente1.HORZ
  N2: A1.D1, Componente1.VERT
  N3: A1.D2, Componente1.SEL
  N4: A1.D3, Mod1.S
  N5: A1.D4, Componente2.SDA
  N6: A1.D5, Componente2.SCL
  N7: A1.D10, U1.DIN
  3V3: A1.3V3, Componente1.VCC, Componente2.VI2C
  GND: A1.GND, U1.GND, Componente1.GND, Mod1.-, Componente2.GND
  5V: A1.5V, U1.VCC, Mod1.NC, Componente2.VDD

notes:
  2x 8x32 Neopixel
  VI2C = 3.3V
  Score Display
  VCC = 5V
  Display HT16K33

custom parts:
  seeeduino-xiao: Seeeduino XIAO processor board SMD version.
  WS2812 RGB LED matrix 8x8: WS2812 matrix 8x8
  14-segment LED Alphanumeric Backpack: This is a nice, bright alphanumeric display that shows letters and numbers. It's super bright and designed for viewing from distances up to 23 feet (7 meters) away. Four digits with 14 segments on a black surface and we give you a set of two alphanumeric displays as well as a driver board so you can make a clock or a four letter word. Like our other LED backpacks, these are end-to-end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
