# Fritzing sketch aula_4_fechadura_simples (saved by Fritzing 1.0.2b)
breadboards: 1

parts:
  Mod1 = Passive Buzzer
  Mod2 = Raspberry Pi Pico
  U1 = Graphical LCD 128x64 [package=lcd-g12864]
  Keypad4x1 = Keypad Membran 4x4
  Mod3 = KY-019 5V Relay Module [package="Breakout board"]

nets:
  N1: Mod1.S, Mod2.pin_1
  N2: Mod1.NC, U1.VSS
  N3: Mod1.-, Mod2.pin_3, Mod2.pin_13, Mod2.pin_33, Mod3.-
  N4: Mod2.pin_4, Keypad4x1.Pin1
  N5: Mod2.pin_5, Keypad4x1.Pin2
  N6: Mod2.pin_6, Keypad4x1.Pin3
  N7: Mod2.pin_12, Mod3.S
  N8: Mod2.pin_14, Mod3.+

custom parts:
  Raspberry Pi Pico: Raspberry Pi Pico. Based around the RP2040 microcontroller the Pico is a low cost microcontroller device bringing Raspberry Pi quality, cost, and easy of use to the microcontroller space. Jan 2021, Split part in to two versions: tht (this one) and SMD. This one will drill holes for a .1 in header in pcb to allow plugging in the module as well as providing pads to solder the module to the top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
  Keypad Membran 4x4: Membrane Keypad 4x4 Matrix
  KY-019 5V Relay Module: KY-019 5V Relay module, used to control AC circuits. (Special thanks to vanepp for fixing the PCB holes and other errors)
