# Fritzing sketch Xiao_Neopixel (saved by Fritzing 1.0.2b)

parts:
  A1 = seeeduino-xiao
  U1 = WS2812 RGB LED matrix 8x8
  Componente1 = Thumb Joystick
  Mod1 = Passive Buzzer
  Grove2 = Grove 4 Digit Display

nets:
  N1: A1.D0, Componente1.HORZ
  N2: A1.D1, Componente1.VERT
  N3: A1.D2, Componente1.SEL
  N4: A1.D3, Mod1.S
  N5: A1.D10, U1.DIN
  3V3: A1.3V3, Componente1.VCC
  GND: A1.GND, U1.GND, Componente1.GND, Mod1.-, Grove2.GND
  VCC: A1.5V, U1.VCC, Mod1.NC, Grove2.VCC

notes:
  2x 8x32 Neopixel
  Score Display

custom parts:
  seeeduino-xiao: Seeeduino XIAO processor board SMD version.
  WS2812 RGB LED matrix 8x8: WS2812 matrix 8x8
